// Logisim project DigitalClock - completo.circ as structural Verilog: 9 circuits, main circuit clock
module _7_seg_display_decode (
  input  D,
  input  C,
  input  B,
  input  A,
  output a_2,
  output b_2,
  output c_2,
  output d_2,
  output e,
  output f,
  output g
);

  wire and_1_out, and_2_out, and_3_out, and_4_out, and_5_out, and_6_out, and_7_out, and_8_out, and_9_out,
       and_10_out, and_11_out, and_12_out, and_13_out, and_14_out, and_15_out, and_16_out, and_17_out,
       not_1_out, not_2_out, not_3_out, not_4_out, not_5_out, not_6_out, not_7_out, not_8_out, not_9_out,
       not_10_out, not_11_out, not_12_out, not_13_out, not_14_out, not_15_out, not_16_out, not_17_out,
       not_18_out, not_19_out, not_20_out, not_21_out, or_1_out, or_2_out, or_3_out, or_4_out, or_6_out,
       or_8_out, or_9_out, or_10_out, or_11_out, or_14_out, or_15_out;

  not not_1 (not_1_out, C);
  and and_1 (and_1_out, not_1_out, not_2_out);
  not not_2 (not_2_out, A);
  and and_2 (and_2_out, C, A);
  not not_3 (not_3_out, C);
  not not_4 (not_4_out, B);
  and and_3 (and_3_out, not_4_out, not_5_out);
  not not_5 (not_5_out, A);
  not not_6 (not_6_out, B);
  or or_1 (or_1_out, not_6_out, A);
  not not_7 (not_7_out, C);
  and and_4 (and_4_out, not_7_out, not_8_out);
  not not_8 (not_8_out, A);
  not not_9 (not_9_out, C);
  and and_5 (and_5_out, not_9_out, B);
  not not_10 (not_10_out, A);
  and and_6 (and_6_out, C, not_11_out);
  not not_11 (not_11_out, B);
  not not_12 (not_12_out, C);
  and and_7 (and_7_out, not_12_out, not_13_out);
  not not_13 (not_13_out, A);
  and and_8 (and_8_out, B, not_14_out);
  not not_14 (not_14_out, A);
  not not_15 (not_15_out, B);
  and and_9 (and_9_out, not_15_out, not_16_out);
  not not_16 (not_16_out, A);
  and and_10 (and_10_out, C, not_17_out);
  not not_17 (not_17_out, B);
  and and_11 (and_11_out, C, not_18_out);
  not not_18 (not_18_out, A);
  not not_19 (not_19_out, C);
  and and_12 (and_12_out, not_19_out, B);
  and and_13 (and_13_out, C, not_20_out);
  not not_20 (not_20_out, B);
  and and_14 (and_14_out, C, not_21_out);
  not not_21 (not_21_out, A);
  or or_2 (or_2_out, and_1_out, B);
  or or_3 (or_3_out, and_2_out, D);
  or or_4 (or_4_out, not_3_out, and_3_out);
  and and_15 (and_15_out, B, A);
  or or_5 (c_2, or_1_out, C);
  or or_6 (or_6_out, and_4_out, and_5_out);
  and and_16 (and_16_out, B, not_10_out);
  and and_17 (and_17_out, and_6_out, A);
  or or_7 (e, and_7_out, and_8_out);
  or or_8 (or_8_out, and_9_out, and_10_out);
  or or_9 (or_9_out, and_11_out, D);
  or or_10 (or_10_out, and_12_out, and_13_out);
  or or_11 (or_11_out, and_14_out, D);
  or or_12 (a_2, or_2_out, or_3_out);
  or or_13 (b_2, or_4_out, and_15_out);
  or or_14 (or_14_out, or_6_out, and_16_out);
  or or_15 (or_15_out, and_17_out, D);
  or or_16 (f, or_8_out, or_9_out);
  or or_17 (g, or_10_out, or_11_out);
  or or_18 (d_2, or_14_out, or_15_out);

  // Notes on the sheet:
  //   THIS IS THE 7 SEGMENT DISPLAY DECODER , it takes a 4 bit input converts it into the signal for the 7 segment display
endmodule

module _0to9_counter__MOD10_counter (
  input  in_1,
  output overflow_to_tens_digit,
  output _8,
  output _4,
  output _2,
  output _1
);

  J_K_Flip_Flop #(.trigger("falling")) FF0_LSB (
    .J(1'b1), .clk(in_1), .K(1'b1), .Q(_1), .reset(overflow_to_tens_digit));  // open: Qn, preset, en
  J_K_Flip_Flop #(.trigger("falling")) FF1 (
    .J(1'b1), .clk(_1), .K(1'b1), .Q(_2), .reset(overflow_to_tens_digit));  // open: Qn, preset, en
  J_K_Flip_Flop #(.trigger("falling")) FF2 (
    .J(1'b1), .clk(_2), .K(1'b1), .Q(_4), .reset(overflow_to_tens_digit));  // open: Qn, preset, en
  J_K_Flip_Flop #(.trigger("falling")) FF3_MSB (
    .J(1'b1), .clk(_4), .K(1'b1), .Q(_8), .reset(overflow_to_tens_digit));  // open: Qn, preset, en
  and and_1 (overflow_to_tens_digit, _2, _8);

  // Notes on the sheet:
  //   This is a MOD 10 Asynchronous Counter using J-K Flip Flops it counts from 0 to 9 and 10 is the reset condition
endmodule

module _0to6_counter__MOD6_counter (
  input  CLK,
  output overflow_to_min_hour,
  output _4,
  output _2,
  output _1
);

  wire not_1_out;

  J_K_Flip_Flop #(.trigger("falling")) FF1_LSB (
    .J(1'b1), .clk(CLK), .K(1'b1), .Q(_1), .reset(overflow_to_min_hour));  // open: Qn, preset, en
  J_K_Flip_Flop #(.trigger("falling")) FF2 (
    .J(1'b1), .clk(_1), .K(1'b1), .Q(_2), .reset(overflow_to_min_hour));  // open: Qn, preset, en
  J_K_Flip_Flop #(.trigger("falling")) FF3_MSB (
    .J(1'b1), .clk(_2), .K(1'b1), .Q(_4), .reset(overflow_to_min_hour));  // open: Qn, preset, en
  not not_1 (not_1_out, _1);
  and and_1 (overflow_to_min_hour, not_1_out, _2, _4);

  // Notes on the sheet:
  //   This is MOD 6 Asynchronous counter which counts from 0 to 5 and 6 is the reset condition
endmodule

module seconds_minutes (
  input  clock,
  output sec_to_min,
  output sec_1__8,
  output sec_1__1,
  output sec_10_4,
  output sec_10_1,
  output sec_1__2,
  output sec_1__4,
  output sec_10_2
);

  wire n0to9_counter_mod10_counter_1_overflow_to_tens_digit;

  _0to6_counter__MOD6_counter u_0to6_counter_mod6_counter_1 (
    .CLK(n0to9_counter_mod10_counter_1_overflow_to_tens_digit), ._4(sec_10_4), ._2(sec_10_2), ._1(sec_10_1),
    .overflow_to_min_hour(sec_to_min));
  _0to9_counter__MOD10_counter u_0to9_counter_mod10_counter_1 (
    .in_1(clock), ._8(sec_1__8), ._4(sec_1__4), ._2(sec_1__2), ._1(sec_1__1),
    .overflow_to_tens_digit(n0to9_counter_mod10_counter_1_overflow_to_tens_digit));

  // Notes on the sheet:
  //   This is the seconds/minutes block it used both MOD6 and MOD10 counter the reset condition for MOD10 counter is used as clock input for MOD6 counter
endmodule

module clock (
);

  wire CLK_out, hours_1_one_s_a, hours_1_one_s_b, hours_1_one_s_c, hours_1_one_s_d, hours_1_one_s_e,
       hours_1_one_s_f, hours_1_one_s_g, hours_1_ten_s_a, hours_1_ten_s_b, hours_1_ten_s_c, hours_1_ten_s_d,
       hours_1_ten_s_e, hours_1_ten_s_f, hours_1_ten_s_g, n7_seg_display_decode_1_a_2,
       n7_seg_display_decode_1_b_2, n7_seg_display_decode_1_c_2, n7_seg_display_decode_1_d_2,
       n7_seg_display_decode_1_e, n7_seg_display_decode_1_f, n7_seg_display_decode_1_g,
       n7_seg_display_decode_2_a_2, n7_seg_display_decode_2_b_2, n7_seg_display_decode_2_c_2,
       n7_seg_display_decode_2_d_2, n7_seg_display_decode_2_e, n7_seg_display_decode_2_f,
       n7_seg_display_decode_2_g, n7_seg_display_decode_3_a_2, n7_seg_display_decode_3_b_2,
       n7_seg_display_decode_3_c_2, n7_seg_display_decode_3_d_2, n7_seg_display_decode_3_e,
       n7_seg_display_decode_3_f, n7_seg_display_decode_3_g, n7_seg_display_decode_4_a_2,
       n7_seg_display_decode_4_b_2, n7_seg_display_decode_4_c_2, n7_seg_display_decode_4_d_2,
       n7_seg_display_decode_4_e, n7_seg_display_decode_4_f, n7_seg_display_decode_4_g,
       seconds_minutes_1_sec_1__1, seconds_minutes_1_sec_1__2, seconds_minutes_1_sec_1__4,
       seconds_minutes_1_sec_1__8, seconds_minutes_1_sec_10_1, seconds_minutes_1_sec_10_2,
       seconds_minutes_1_sec_10_4, seconds_minutes_1_sec_to_min, seconds_minutes_2_sec_1__1,
       seconds_minutes_2_sec_1__2, seconds_minutes_2_sec_1__4, seconds_minutes_2_sec_1__8,
       seconds_minutes_2_sec_10_1, seconds_minutes_2_sec_10_2, seconds_minutes_2_sec_10_4,
       seconds_minutes_2_sec_to_min;

  hours hours_1 (
    .CLK_from_min(seconds_minutes_1_sec_to_min), .one_s_a(hours_1_one_s_a), .one_s_b(hours_1_one_s_b),
    .one_s_c(hours_1_one_s_c), .one_s_d(hours_1_one_s_d), .one_s_e(hours_1_one_s_e),
    .one_s_f(hours_1_one_s_f), .one_s_g(hours_1_one_s_g), .ten_s_a(hours_1_ten_s_a),
    .ten_s_b(hours_1_ten_s_b), .ten_s_c(hours_1_ten_s_c), .ten_s_d(hours_1_ten_s_d),
    .ten_s_e(hours_1_ten_s_e), .ten_s_f(hours_1_ten_s_f), .ten_s_g(hours_1_ten_s_g));
  _7_Segment_Display u_7_segment_display_1 (
    .g(hours_1_ten_s_g), .f(hours_1_ten_s_f), .a(hours_1_ten_s_a), .b(hours_1_ten_s_b), .e(hours_1_ten_s_e),
    .d(hours_1_ten_s_d), .c(hours_1_ten_s_c));  // open: dp
  _7_Segment_Display u_7_segment_display_2 (
    .g(hours_1_one_s_g), .f(hours_1_one_s_f), .a(hours_1_one_s_a), .b(hours_1_one_s_b), .e(hours_1_one_s_e),
    .d(hours_1_one_s_d), .c(hours_1_one_s_c));  // open: dp
  _7_seg_display_decode u_7_seg_display_decode_1 (
    .D(1'b0), .C(seconds_minutes_1_sec_10_4), .B(seconds_minutes_1_sec_10_2), .A(seconds_minutes_1_sec_10_1),
    .a_2(n7_seg_display_decode_1_a_2), .b_2(n7_seg_display_decode_1_b_2), .c_2(n7_seg_display_decode_1_c_2),
    .d_2(n7_seg_display_decode_1_d_2), .e(n7_seg_display_decode_1_e), .f(n7_seg_display_decode_1_f),
    .g(n7_seg_display_decode_1_g));
  seconds_minutes seconds_minutes_1 (
    .clock(seconds_minutes_2_sec_to_min), .sec_10_4(seconds_minutes_1_sec_10_4),
    .sec_10_2(seconds_minutes_1_sec_10_2), .sec_10_1(seconds_minutes_1_sec_10_1),
    .sec_1__8(seconds_minutes_1_sec_1__8), .sec_1__4(seconds_minutes_1_sec_1__4),
    .sec_1__2(seconds_minutes_1_sec_1__2), .sec_1__1(seconds_minutes_1_sec_1__1),
    .sec_to_min(seconds_minutes_1_sec_to_min));
  _7_seg_display_decode u_7_seg_display_decode_2 (
    .D(seconds_minutes_1_sec_1__8), .C(seconds_minutes_1_sec_1__4), .B(seconds_minutes_1_sec_1__2),
    .A(seconds_minutes_1_sec_1__1), .a_2(n7_seg_display_decode_2_a_2), .b_2(n7_seg_display_decode_2_b_2),
    .c_2(n7_seg_display_decode_2_c_2), .d_2(n7_seg_display_decode_2_d_2), .e(n7_seg_display_decode_2_e),
    .f(n7_seg_display_decode_2_f), .g(n7_seg_display_decode_2_g));
  _7_Segment_Display u_7_segment_display_3 (
    .g(n7_seg_display_decode_2_g), .f(n7_seg_display_decode_2_f), .a(n7_seg_display_decode_2_a_2),
    .b(n7_seg_display_decode_2_b_2), .e(n7_seg_display_decode_2_e), .d(n7_seg_display_decode_2_d_2),
    .c(n7_seg_display_decode_2_c_2));  // open: dp
  _7_Segment_Display u_7_segment_display_4 (
    .g(n7_seg_display_decode_1_g), .f(n7_seg_display_decode_1_f), .a(n7_seg_display_decode_1_a_2),
    .b(n7_seg_display_decode_1_b_2), .e(n7_seg_display_decode_1_e), .d(n7_seg_display_decode_1_d_2),
    .c(n7_seg_display_decode_1_c_2));  // open: dp
  Clock #(.highDuration(2), .lowDuration(2)) CLK (.out(CLK_out));
  seconds_minutes seconds_minutes_2 (
    .clock(CLK_out), .sec_10_4(seconds_minutes_2_sec_10_4), .sec_10_2(seconds_minutes_2_sec_10_2),
    .sec_10_1(seconds_minutes_2_sec_10_1), .sec_1__8(seconds_minutes_2_sec_1__8),
    .sec_1__4(seconds_minutes_2_sec_1__4), .sec_1__2(seconds_minutes_2_sec_1__2),
    .sec_1__1(seconds_minutes_2_sec_1__1), .sec_to_min(seconds_minutes_2_sec_to_min));
  _7_seg_display_decode u_7_seg_display_decode_3 (
    .D(1'b0), .C(seconds_minutes_2_sec_10_4), .B(seconds_minutes_2_sec_10_2), .A(seconds_minutes_2_sec_10_1),
    .a_2(n7_seg_display_decode_3_a_2), .b_2(n7_seg_display_decode_3_b_2), .c_2(n7_seg_display_decode_3_c_2),
    .d_2(n7_seg_display_decode_3_d_2), .e(n7_seg_display_decode_3_e), .f(n7_seg_display_decode_3_f),
    .g(n7_seg_display_decode_3_g));
  _7_seg_display_decode u_7_seg_display_decode_4 (
    .D(seconds_minutes_2_sec_1__8), .C(seconds_minutes_2_sec_1__4), .B(seconds_minutes_2_sec_1__2),
    .A(seconds_minutes_2_sec_1__1), .a_2(n7_seg_display_decode_4_a_2), .b_2(n7_seg_display_decode_4_b_2),
    .c_2(n7_seg_display_decode_4_c_2), .d_2(n7_seg_display_decode_4_d_2), .e(n7_seg_display_decode_4_e),
    .f(n7_seg_display_decode_4_f), .g(n7_seg_display_decode_4_g));
  _7_Segment_Display u_7_segment_display_5 (
    .g(n7_seg_display_decode_3_g), .f(n7_seg_display_decode_3_f), .a(n7_seg_display_decode_3_a_2),
    .b(n7_seg_display_decode_3_b_2), .e(n7_seg_display_decode_3_e), .d(n7_seg_display_decode_3_d_2),
    .c(n7_seg_display_decode_3_c_2));  // open: dp
  _7_Segment_Display u_7_segment_display_6 (
    .g(n7_seg_display_decode_4_g), .f(n7_seg_display_decode_4_f), .a(n7_seg_display_decode_4_a_2),
    .b(n7_seg_display_decode_4_b_2), .e(n7_seg_display_decode_4_e), .d(n7_seg_display_decode_4_d_2),
    .c(n7_seg_display_decode_4_c_2));  // open: dp

  // Notes on the sheet:
  //   HOURS
  //   The final clock with minutes . seconds and hours 
  //   The hours block clock input is the reset condition for minutes block
  //   Global reset occurs when the clock reaches 23:59:59
  //   MINUTES BLOCK
  //   The minutes block is same as the seconds block with only difference the clock input for minutes block being the reset condition for seconds block
  //   MINUTES
  //   SECONDS BLOCK
  //   SECONDS
endmodule

module _0to23_counter__MOD24_counter (
  input  Clock,
  output s0,
  output s1,
  output s2,
  output s3,
  output s4,
  output s5,
  output overflow
);

  wire not_1_out, not_2_out, not_3_out, not_4_out, t_ff_1_qn, t_ff_2_qn, t_ff_3_qn, t_ff_4_qn, t_ff_5_qn;

  and and_1 (overflow, not_1_out, not_2_out, not_3_out, s3, s4, not_4_out);
  T_Flip_Flop t_ff_1 (.clk(Clock), .T(1'b1), .Q(s0), .Qn(t_ff_1_qn), .reset(overflow));  // open: preset, en
  T_Flip_Flop t_ff_2 (.clk(t_ff_1_qn), .T(1'b1), .Q(s1), .Qn(t_ff_2_qn), .reset(overflow));  // open: preset, en
  T_Flip_Flop t_ff_3 (.clk(t_ff_2_qn), .T(1'b1), .Q(s2), .Qn(t_ff_3_qn), .reset(overflow));  // open: preset, en
  T_Flip_Flop t_ff_4 (.clk(t_ff_3_qn), .T(1'b1), .Q(s3), .Qn(t_ff_4_qn), .reset(overflow));  // open: preset, en
  T_Flip_Flop t_ff_5 (.clk(t_ff_4_qn), .T(1'b1), .Q(s4), .Qn(t_ff_5_qn), .reset(overflow));  // open: preset, en
  T_Flip_Flop t_ff_6 (.clk(t_ff_5_qn), .T(1'b1), .Q(s5), .reset(overflow));  // open: Qn, preset, en
  not not_1 (not_1_out, s0);
  not not_2 (not_2_out, s1);
  not not_3 (not_3_out, s2);
  not not_4 (not_4_out, s5);

  // Notes on the sheet:
  //   This is a 6bit MOD24 counter which counts from 0 to 23 and 24 is the reset condition
endmodule

module _6bit_to_4bit_ones_place (
  input  a,
  input  b,
  input  c,
  input  d,
  input  e,
  input  f,
  output D_2,
  output C_2,
  output B_2,
  output A_2
);

  wire and_1_out, and_2_out, and_3_out, and_4_out, and_5_out, and_6_out, and_7_out, and_8_out, and_9_out,
       and_10_out, and_11_out, and_12_out, and_13_out, and_14_out, and_15_out, and_16_out, and_17_out,
       and_18_out, and_19_out, and_20_out, and_21_out, and_22_out, and_23_out, not_1_out, not_2_out,
       not_3_out, not_4_out, not_5_out, not_6_out, not_7_out, not_8_out, not_9_out, not_10_out, not_11_out,
       not_12_out, not_13_out, not_14_out, not_15_out, not_16_out, not_17_out, not_18_out, not_19_out,
       not_20_out, not_21_out, not_22_out, not_23_out, not_24_out, not_25_out, not_26_out, not_27_out,
       not_28_out, not_29_out, not_30_out, not_31_out, not_32_out, not_33_out, not_34_out, not_35_out,
       not_36_out, not_37_out, not_38_out, not_39_out, not_40_out, not_41_out, not_42_out, not_43_out,
       not_44_out, not_45_out, not_46_out, not_47_out, not_48_out, not_49_out;

  not not_1 (not_1_out, a);
  not not_2 (not_2_out, b);
  not not_3 (not_3_out, d);
  not not_4 (not_4_out, e);
  not not_5 (not_5_out, a);
  not not_6 (not_6_out, c);
  not not_7 (not_7_out, d);
  not not_8 (not_8_out, e);
  not not_9 (not_9_out, b);
  not not_10 (not_10_out, c);
  not not_11 (not_11_out, c);
  not not_12 (not_12_out, d);
  not not_13 (not_13_out, e);
  not not_14 (not_14_out, b);
  not not_15 (not_15_out, c);
  not not_16 (not_16_out, e);
  not not_17 (not_17_out, a);
  not not_18 (not_18_out, b);
  not not_19 (not_19_out, a);
  not not_20 (not_20_out, d);
  not not_21 (not_21_out, e);
  not not_22 (not_22_out, a);
  not not_23 (not_23_out, d);
  not not_24 (not_24_out, d);
  not not_25 (not_25_out, e);
  not not_26 (not_26_out, b);
  not not_27 (not_27_out, c);
  not not_28 (not_28_out, d);
  not not_29 (not_29_out, a);
  not not_30 (not_30_out, b);
  not not_31 (not_31_out, c);
  not not_32 (not_32_out, a);
  not not_33 (not_33_out, c);
  not not_34 (not_34_out, a);
  not not_35 (not_35_out, b);
  not not_36 (not_36_out, e);
  not not_37 (not_37_out, a);
  not not_38 (not_38_out, c);
  not not_39 (not_39_out, d);
  not not_40 (not_40_out, e);
  not not_41 (not_41_out, a);
  not not_42 (not_42_out, d);
  not not_43 (not_43_out, b);
  not not_44 (not_44_out, c);
  not not_45 (not_45_out, e);
  not not_46 (not_46_out, c);
  not not_47 (not_47_out, e);
  not not_48 (not_48_out, b);
  not not_49 (not_49_out, e);
  and and_1 (and_1_out, not_1_out, not_2_out, c, not_3_out, not_4_out);
  and and_2 (and_2_out, not_5_out, b, not_6_out, not_7_out, e);
  and and_3 (and_3_out, b, c, d, not_8_out);
  and and_4 (and_4_out, a, not_9_out, not_10_out, d, e);
  and and_5 (and_5_out, a, b, not_11_out, not_12_out, not_13_out);
  and and_6 (and_6_out, a, b, c, e);
  and and_7 (and_7_out, not_14_out, not_15_out, d, not_16_out);
  and and_8 (and_8_out, not_17_out, not_18_out, d, e);
  and and_9 (and_9_out, not_19_out, b, not_20_out, not_21_out);
  and and_10 (and_10_out, not_22_out, b, c, not_23_out);
  and and_11 (and_11_out, b, c, not_24_out, not_25_out);
  and and_12 (and_12_out, a, not_26_out, not_27_out, not_28_out, e);
  and and_13 (and_13_out, a, c, d);
  and and_14 (and_14_out, a, b, d, e);
  and and_15 (and_15_out, not_29_out, not_30_out, not_31_out, e);
  and and_16 (and_16_out, not_32_out, not_33_out, d, e);
  and and_17 (and_17_out, not_34_out, not_35_out, c, d, not_36_out);
  and and_18 (and_18_out, not_37_out, b, not_38_out, not_39_out, not_40_out);
  and and_19 (and_19_out, not_41_out, b, c, not_42_out, e);
  and and_20 (and_20_out, a, not_43_out, not_44_out, not_45_out);
  and and_21 (and_21_out, a, not_46_out, d, not_47_out);
  and and_22 (and_22_out, a, not_48_out, c, e);
  and and_23 (and_23_out, a, b, c, not_49_out);
  or or_1 (D_2, and_1_out, and_2_out, and_3_out, and_4_out, and_5_out, and_6_out);
  or or_2 (C_2, and_7_out, and_8_out, and_9_out, and_10_out, and_11_out, and_12_out, and_13_out, and_14_out);
  or or_3 (B_2, and_15_out, and_16_out, and_17_out, and_18_out, and_19_out, and_20_out, and_21_out, and_22_out, and_23_out);

  assign A_2 = f;

  // Notes on the sheet:
  //   This is a converter used for taking a 6bit 2 digit number as input and returning a 4bit equivalent of the one's place of the number
endmodule

module _6bit_to_4bit_tensplace (
  input  a,
  input  b,
  input  c,
  input  d,
  input  e,
  input  f,
  output D_2,
  output C_2,
  output B_2,
  output A_2
);

  wire and_1_out, and_2_out, and_3_out, and_4_out, and_5_out, and_6_out, and_7_out, and_8_out, and_9_out,
       and_10_out, and_11_out, and_12_out, and_13_out, not_1_out, not_2_out, not_3_out, not_4_out, not_5_out,
       not_6_out, not_7_out, not_8_out, not_9_out, not_10_out, not_11_out, not_12_out, not_13_out,
       not_14_out, not_15_out, not_16_out;

  and and_1 (and_1_out, a, c);
  and and_2 (and_2_out, a, b);
  not not_1 (not_1_out, a);
  not not_2 (not_2_out, a);
  not not_3 (not_3_out, b);
  not not_4 (not_4_out, c);
  not not_5 (not_5_out, a);
  not not_6 (not_6_out, b);
  not not_7 (not_7_out, a);
  not not_8 (not_8_out, b);
  not not_9 (not_9_out, a);
  not not_10 (not_10_out, a);
  not not_11 (not_11_out, c);
  not not_12 (not_12_out, d);
  not not_13 (not_13_out, b);
  not not_14 (not_14_out, c);
  not not_15 (not_15_out, c);
  not not_16 (not_16_out, c);
  or or_1 (C_2, and_1_out, and_2_out);
  and and_3 (and_3_out, not_1_out, b, d);
  and and_4 (and_4_out, not_2_out, b, c);
  and and_5 (and_5_out, a, not_3_out, not_4_out);
  and and_6 (and_6_out, not_5_out, not_6_out, c, e);
  and and_7 (and_7_out, not_7_out, not_8_out, c, d);
  and and_8 (and_8_out, not_9_out, c, d, e);
  and and_9 (and_9_out, not_10_out, b, not_11_out, not_12_out);
  and and_10 (and_10_out, a, not_13_out, not_14_out);
  and and_11 (and_11_out, a, not_15_out, e);
  and and_12 (and_12_out, a, not_16_out, d);
  and and_13 (and_13_out, a, b, c);
  or or_2 (B_2, and_3_out, and_4_out, and_5_out);
  or or_3 (A_2, and_6_out, and_7_out, and_8_out, and_9_out, and_10_out, and_11_out, and_12_out, and_13_out);

  assign D_2 = 1'b0;

  // Notes on the sheet:
  //   This is a converter which takes 6bit 2 digit number input and returns 4bit ten' place of the number
endmodule

// HOURS BLOCK
module hours (
  input  CLK_from_min,
  output one_s_a,
  output one_s_b,
  output one_s_c,
  output one_s_d,
  output one_s_e,
  output one_s_f,
  output one_s_g,
  output ten_s_a,
  output ten_s_b,
  output ten_s_c,
  output ten_s_d,
  output ten_s_e,
  output ten_s_f,
  output ten_s_g
);

  wire n0to23_counter_mod24_counter_1_s0, n0to23_counter_mod24_counter_1_s1,
       n0to23_counter_mod24_counter_1_s2, n0to23_counter_mod24_counter_1_s3,
       n0to23_counter_mod24_counter_1_s4, n0to23_counter_mod24_counter_1_s5, n6bit_to_4bit_ones_place_1_a_2,
       n6bit_to_4bit_ones_place_1_b_2, n6bit_to_4bit_ones_place_1_c_2, n6bit_to_4bit_ones_place_1_d_2,
       n6bit_to_4bit_tensplace_1_a_2, n6bit_to_4bit_tensplace_1_b_2, n6bit_to_4bit_tensplace_1_c_2,
       n6bit_to_4bit_tensplace_1_d_2;

  _0to23_counter__MOD24_counter u_0to23_counter_mod24_counter_1 (
    .Clock(CLK_from_min), .s0(n0to23_counter_mod24_counter_1_s0), .s1(n0to23_counter_mod24_counter_1_s1),
    .s2(n0to23_counter_mod24_counter_1_s2), .s3(n0to23_counter_mod24_counter_1_s3),
    .s4(n0to23_counter_mod24_counter_1_s4), .s5(n0to23_counter_mod24_counter_1_s5));  // open: overflow
  _6bit_to_4bit_ones_place u_6bit_to_4bit_ones_place_1 (
    .a(n0to23_counter_mod24_counter_1_s5), .b(n0to23_counter_mod24_counter_1_s4),
    .c(n0to23_counter_mod24_counter_1_s3), .d(n0to23_counter_mod24_counter_1_s2),
    .e(n0to23_counter_mod24_counter_1_s1), .f(n0to23_counter_mod24_counter_1_s0),
    .D_2(n6bit_to_4bit_ones_place_1_d_2), .C_2(n6bit_to_4bit_ones_place_1_c_2),
    .B_2(n6bit_to_4bit_ones_place_1_b_2), .A_2(n6bit_to_4bit_ones_place_1_a_2));
  _6bit_to_4bit_tensplace u_6bit_to_4bit_tensplace_1 (
    .a(n0to23_counter_mod24_counter_1_s5), .b(n0to23_counter_mod24_counter_1_s4),
    .c(n0to23_counter_mod24_counter_1_s3), .d(n0to23_counter_mod24_counter_1_s2),
    .e(n0to23_counter_mod24_counter_1_s1), .f(n0to23_counter_mod24_counter_1_s0),
    .D_2(n6bit_to_4bit_tensplace_1_d_2), .C_2(n6bit_to_4bit_tensplace_1_c_2),
    .B_2(n6bit_to_4bit_tensplace_1_b_2), .A_2(n6bit_to_4bit_tensplace_1_a_2));
  _7_seg_display_decode u_7_seg_display_decode_1 (
    .D(n6bit_to_4bit_ones_place_1_d_2), .C(n6bit_to_4bit_ones_place_1_c_2),
    .B(n6bit_to_4bit_ones_place_1_b_2), .A(n6bit_to_4bit_ones_place_1_a_2), .a_2(one_s_a), .b_2(one_s_b),
    .c_2(one_s_c), .d_2(one_s_d), .e(one_s_e), .f(one_s_f), .g(one_s_g));
  _7_seg_display_decode u_7_seg_display_decode_2 (
    .D(n6bit_to_4bit_tensplace_1_d_2), .C(n6bit_to_4bit_tensplace_1_c_2), .B(n6bit_to_4bit_tensplace_1_b_2),
    .A(n6bit_to_4bit_tensplace_1_a_2), .a_2(ten_s_a), .b_2(ten_s_b), .c_2(ten_s_c), .d_2(ten_s_d),
    .e(ten_s_e), .f(ten_s_f), .g(ten_s_g));

  // Notes on the sheet:
  //   This is the hours block it includes the MOD 24 counter along with one's place and ten's place circuits with display decoder 
endmodule
