// Logisim project Relogio Digital decodificador semipronto.circ as structural Verilog
module Relogio (
);

  wire clock_1_out, clock_2_out, contador_0_59_1_prox_clk, contador_0_59_2_prox_clk, Reset_out;
  wire [3:0] contador_0_23_1_dezena, contador_0_23_1_unidade, contador_0_59_1_dezena,
       contador_0_59_1_unidade, contador_0_59_2_dezena, contador_0_59_2_unidade;

  Hex_Digit_Display hex_digit_display_1 (.value(contador_0_23_1_dezena));  // open: dp
  LED led_1 (.in(1'b1));
  LED led_2 (.in(1'b1));
  Hex_Digit_Display hex_digit_display_2 (.value(contador_0_23_1_unidade));  // open: dp
  Contador_0_23 contador_0_23_1 (
    .Dezena(contador_0_23_1_dezena), .CLK(contador_0_59_1_prox_clk), .Unidade(contador_0_23_1_unidade),
    .Reset(Reset_out));  // open: Prox_CLK
  Hex_Digit_Display hex_digit_display_3 (.value(contador_0_59_1_unidade));  // open: dp
  Hex_Digit_Display hex_digit_display_4 (.value(contador_0_59_1_dezena));  // open: dp
  Contador_0_59 contador_0_59_1 (
    .Dezena(contador_0_59_1_dezena), .CLK(contador_0_59_2_prox_clk), .Unidade(contador_0_59_1_unidade),
    .Prox_CLK(contador_0_59_1_prox_clk), .Reset(Reset_out));
  Clock clock_1 (.out(clock_1_out));
  LED led_3 (.in(clock_1_out));
  LED led_4 (.in(clock_1_out));
  Hex_Digit_Display hex_digit_display_5 (.value(contador_0_59_2_dezena));  // open: dp
  Clock clock_2 (.out(clock_2_out));
  Hex_Digit_Display hex_digit_display_6 (.value(contador_0_59_2_unidade));  // open: dp
  Contador_0_59 contador_0_59_2 (
    .Dezena(contador_0_59_2_dezena), .CLK(clock_2_out), .Unidade(contador_0_59_2_unidade),
    .Prox_CLK(contador_0_59_2_prox_clk), .Reset(Reset_out));
  Button Reset (.out(Reset_out));
endmodule

module Contador_0_9 (
  input  CLK,
  input  Reset,
  output [3:0] \Saída ,
  output Prox_CLK
);

  wire or_1_out;
  wire [3:0] adder_1_out;

  Register #(.width(4)) register_1 (.D(adder_1_out), .Q(\Saída ), .clk(CLK), .clr(or_1_out));  // open: en
  or or_1 (or_1_out, Prox_CLK, Reset);
  Hex_Digit_Display hex_digit_display_1 (.value(\Saída ));  // open: dp
  Adder #(.width(4)) adder_1 (.a(\Saída ), .b(4'b0001), .out(adder_1_out));  // open: cin, cout
  and and_1 (Prox_CLK, \Saída [1], \Saída [3]);
endmodule

module Contador_0_59 (
  input  CLK,
  input  Reset,
  output [3:0] Dezena,
  output [3:0] Unidade,
  output Prox_CLK
);

  wire contador_0_9_2_prox_clk, or_1_out;

  or or_1 (or_1_out, Reset, Prox_CLK);
  Hex_Digit_Display hex_digit_display_1 (.value(Dezena));  // open: dp
  Contador_0_9 contador_0_9_1 (.CLK(contador_0_9_2_prox_clk), .Reset(or_1_out), .\Saída (Dezena));  // open: Prox_CLK
  Hex_Digit_Display hex_digit_display_2 (.value(Unidade));  // open: dp
  Contador_0_9 contador_0_9_2 (.CLK(CLK), .Reset(or_1_out), .\Saída (Unidade), .Prox_CLK(contador_0_9_2_prox_clk));
  nor nor_1 (Prox_CLK, Dezena[3], ~Dezena[2], ~Dezena[1], Dezena[0], Unidade[3], Unidade[2], Unidade[1], Unidade[0]);  // NOR_Gate
endmodule

module Contador_0_23 (
  input  CLK,
  input  Reset,
  output [3:0] Dezena,
  output [3:0] Unidade,
  output Prox_CLK
);

  wire contador_0_9_2_prox_clk, or_1_out;

  or or_1 (or_1_out, Reset, Prox_CLK);
  Hex_Digit_Display hex_digit_display_1 (.value(Dezena));  // open: dp
  Contador_0_9 contador_0_9_1 (.CLK(contador_0_9_2_prox_clk), .Reset(or_1_out), .\Saída (Dezena));  // open: Prox_CLK
  Hex_Digit_Display hex_digit_display_2 (.value(Unidade));  // open: dp
  Contador_0_9 contador_0_9_2 (.CLK(CLK), .Reset(or_1_out), .\Saída (Unidade), .Prox_CLK(contador_0_9_2_prox_clk));
  nor nor_1 (Prox_CLK, Dezena[3], Dezena[2], ~Dezena[1], Dezena[0], Unidade[3], ~Unidade[2], Unidade[1], Unidade[0]);  // NOR_Gate
endmodule

module decodificador (
  input  A,
  input  A_2,
  input  B,
  input  B_2,
  input  C,
  input  C_2,
  input  D,
  input  D_2,
  input  A_3,
  input  A_4,
  input  B_3,
  input  B_4,
  input  C_3,
  input  C_4,
  input  D_3,
  input  D_4,
  input  A_5,
  input  A_6,
  input  B_5,
  input  B_6,
  input  C_5,
  input  C_6,
  input  D_5,
  input  D_6,
  input  A_7,
  input  B_7,
  input  C_7,
  input  D_7,
  output a_8,
  output e,
  output f,
  output b_8,
  output c_8,
  output g,
  output d_8
);

  wire and_1_out, and_2_out, and_3_out, and_4_out, and_5_out, and_6_out, and_7_out, and_8_out, and_9_out,
       and_10_out, and_11_out, and_12_out, and_13_out, and_14_out, and_15_out, and_16_out, and_17_out,
       and_18_out, and_19_out, and_20_out, and_21_out, and_22_out, and_23_out, and_24_out, and_25_out,
       and_26_out, and_27_out, and_28_out, not_1_out, not_2_out, not_3_out, not_4_out, not_5_out, not_6_out,
       not_7_out, not_8_out, not_9_out, not_10_out, not_11_out, not_12_out, not_13_out, not_14_out,
       not_15_out, not_16_out, not_17_out, not_18_out, not_19_out, not_20_out, not_21_out, not_22_out,
       not_23_out, not_24_out, not_25_out, not_26_out, not_27_out, not_28_out, not_29_out, not_30_out,
       not_31_out, not_32_out, not_33_out, not_34_out, not_35_out, not_36_out, not_37_out, not_38_out,
       not_39_out, not_40_out, not_41_out, not_42_out, not_43_out, not_44_out, not_45_out, not_46_out,
       not_47_out, not_48_out, not_49_out, not_50_out, not_51_out, not_52_out, not_53_out, not_54_out,
       not_55_out, not_56_out;

  not not_1 (not_1_out, A);
  not not_2 (not_2_out, A);
  not not_3 (not_3_out, B);
  not not_4 (not_4_out, C);
  not not_5 (not_5_out, D);
  not not_6 (not_6_out, B);
  not not_7 (not_7_out, A_4);
  not not_8 (not_8_out, B_4);
  not not_9 (not_9_out, A_4);
  not not_10 (not_10_out, A_4);
  not not_11 (not_11_out, C_4);
  not not_12 (not_12_out, D_4);
  not not_13 (not_13_out, B_4);
  not not_14 (not_14_out, C_4);
  not not_15 (not_15_out, A_6);
  not not_16 (not_16_out, C_6);
  not not_17 (not_17_out, A_6);
  not not_18 (not_18_out, A_6);
  not not_19 (not_19_out, B_6);
  not not_20 (not_20_out, C_6);
  not not_21 (not_21_out, A_7);
  not not_22 (not_22_out, B_7);
  not not_23 (not_23_out, A_7);
  not not_24 (not_24_out, D_7);
  not not_25 (not_25_out, A_7);
  not not_26 (not_26_out, C_7);
  not not_27 (not_27_out, B_7);
  not not_28 (not_28_out, C_7);
  not not_29 (not_29_out, D_7);
  not not_30 (not_30_out, B_7);
  not not_31 (not_31_out, C_7);
  and and_1 (and_1_out, not_1_out, C);
  and and_2 (and_2_out, not_2_out, B, D);
  and and_3 (and_3_out, not_3_out, not_4_out, not_5_out);
  and and_4 (and_4_out, A, not_6_out, D);
  and and_5 (and_5_out, not_7_out, not_8_out);
  and and_6 (and_6_out, not_9_out, C_4, D_4);
  and and_7 (and_7_out, not_10_out, not_11_out, not_12_out);
  and and_8 (and_8_out, A_4, not_13_out, not_14_out);
  and and_9 (and_9_out, not_15_out, not_16_out);
  and and_10 (and_10_out, not_17_out, D_6);
  and and_11 (and_11_out, not_18_out, B_6);
  and and_12 (and_12_out, not_19_out, not_20_out);
  and and_13 (and_13_out, not_21_out, not_22_out, C_7);
  and and_14 (and_14_out, not_23_out, C_7, not_24_out);
  and and_15 (and_15_out, not_25_out, B_7, not_26_out, D_7);
  and and_16 (and_16_out, not_27_out, not_28_out, not_29_out);
  and and_17 (and_17_out, A_7, not_30_out, not_31_out);
  or or_1 (a_8, and_1_out, and_2_out, and_3_out, and_4_out);
  or or_2 (b_8, and_5_out, and_6_out, and_7_out, and_8_out);
  or or_3 (c_8, and_9_out, and_10_out, and_11_out, and_12_out);
  or or_4 (d_8, and_13_out, and_14_out, and_15_out, and_16_out, and_17_out);
  not not_32 (not_32_out, A_2);
  not not_33 (not_33_out, B_2);
  not not_34 (not_34_out, D_2);
  not not_35 (not_35_out, A_2);
  not not_36 (not_36_out, D_2);
  not not_37 (not_37_out, B_2);
  not not_38 (not_38_out, D_2);
  not not_39 (not_39_out, C_2);
  not not_40 (not_40_out, A_3);
  not not_41 (not_41_out, C_3);
  not not_42 (not_42_out, D_3);
  not not_43 (not_43_out, A_3);
  not not_44 (not_44_out, C_3);
  not not_45 (not_45_out, A_3);
  not not_46 (not_46_out, D_3);
  not not_47 (not_47_out, B_3);
  not not_48 (not_48_out, C_3);
  not not_49 (not_49_out, A_5);
  not not_50 (not_50_out, B_5);
  not not_51 (not_51_out, A_5);
  not not_52 (not_52_out, D_5);
  not not_53 (not_53_out, A_5);
  not not_54 (not_54_out, C_5);
  not not_55 (not_55_out, B_5);
  not not_56 (not_56_out, C_5);
  and and_18 (and_18_out, not_32_out, not_33_out, not_34_out);
  and and_19 (and_19_out, not_35_out, C_2, not_36_out);
  and and_20 (and_20_out, not_37_out, not_38_out, not_39_out);
  and and_21 (and_21_out, not_40_out, not_41_out, not_42_out);
  and and_22 (and_22_out, not_43_out, B_3, not_44_out);
  and and_23 (and_23_out, not_45_out, B_3, not_46_out);
  and and_24 (and_24_out, A_3, not_47_out, not_48_out);
  and and_25 (and_25_out, not_49_out, not_50_out, C_5);
  and and_26 (and_26_out, not_51_out, C_5, not_52_out);
  and and_27 (and_27_out, not_53_out, B_5, not_54_out);
  and and_28 (and_28_out, A_5, not_55_out, not_56_out);
  or or_5 (e, and_18_out, and_19_out, and_20_out);
  or or_6 (f, and_21_out, and_22_out, and_23_out, and_24_out);
  or or_7 (g, and_25_out, and_26_out, and_27_out, and_28_out);
endmodule
