// Logisim project circuito_01.circ as structural Verilog: 2 circuits, main circuit primeiro
module primeiro (
  input  A,
  input  B,
  input  C,
  output out_4
);

  wire and_1_out, and_2_out;

  and and_1 (and_1_out, ~A, ~C);  // AND_Gate
  and and_2 (and_2_out, B, C);
  or or_1 (out_4, and_1_out, and_2_out);

  // Notes on the sheet:
  //   Circuito 01
  //   S=(A'.C') + (B.C)
endmodule

module segundo (
);

  primeiro primeiro_1 ();  // open: A, B, C, out_4
endmodule
